// Logisim project cache_simulation.circ as structural Verilog: 4 circuits, main circuit main
module main (
);

  wire cache_1_done, cache_1_memoryenable, cache_1_memoryweout, clk_out, cpu_1_we, memory_1_done;
  wire [7:0] cache_1_dataout, memory_1_dataout;
  wire [31:0] cache_1_memoryaddressout, cache_1_memorydataout, cpu_1_address, cpu_1_data;

  Clock clk (.out(clk_out));
  cpu cpu_1 (
    .clk(clk_out), .cacheDone(cache_1_done), .cacheReadData(cache_1_dataout), .address(cpu_1_address),
    .data(cpu_1_data), .we(cpu_1_we));
  cache cache_1 (
    .clk(clk_out), .address(cpu_1_address), .dataIn(cpu_1_data), .we(cpu_1_we),
    .memoryDataIn(memory_1_dataout), .memoryDone(memory_1_done), .dataOut(cache_1_dataout),
    .done(cache_1_done), .memoryAddressOut(cache_1_memoryaddressout), .memoryDataOut(cache_1_memorydataout),
    .memoryWeOut(cache_1_memoryweout), .memoryEnable(cache_1_memoryenable));
  memory memory_1 (
    .clk(clk_out), .address(cache_1_memoryaddressout), .data(cache_1_memorydataout),
    .we(cache_1_memoryweout), .memoryEnable(cache_1_memoryenable), .dataOut(memory_1_dataout),
    .done(memory_1_done));
endmodule

module cpu (
  input  clk,
  input  cacheDone,
  input  [7:0] cacheReadData,
  output [31:0] address,
  output [31:0] data,
  output we
);
endmodule

module cache (
  input  clk,
  input  [31:0] address,
  input  [31:0] dataIn,
  input  we,
  input  [7:0] memoryDataIn,
  input  memoryDone,
  output [7:0] dataOut,
  output done,
  output [31:0] memoryAddressOut,
  output [31:0] memoryDataOut,
  output memoryWeOut,
  output memoryEnable
);
endmodule

module memory (
  input  clk,
  input  [31:0] address,
  input  [31:0] data,
  input  we,
  input  memoryEnable,
  output [7:0] dataOut,
  output done
);
endmodule
